# Fritzing sketch smartroomcontrollercircuitry (saved by Fritzing 0.9.9b)
breadboards: 1

parts:
  Part1 = Adafruit MAX4466 Electret Microphone Amplifier [part_number="Adafruit #1063"]
  WIZ820io1 = WIZ820io [part_number=WIZ820io]
  M1 = BMP280
  OLED_I2C1 = OLED 128x64 I2C Monochrome Display
  U1 = ENCODER_RGB [package=encoder_led_2]
  Teensy_3_1 = Teensy 3.1

nets:
  VIN: Part1.VCC, WIZ820io1.VIN, M1.VIN, OLED_I2C1.VDD, Teensy_3_1.3V3
  GND: Part1.GND, WIZ820io1.GND, M1.GND, OLED_I2C1.GND, U1.C, Teensy_3_1.GND
  N1: Part1.OUT, Teensy_3_1.A9/D23
  N2: WIZ820io1.MOSI, Teensy_3_1.D11
  N3: WIZ820io1.SCLK, Teensy_3_1.D13
  N4: WIZ820io1.nSS, Teensy_3_1.D10
  N5: WIZ820io1.MISO, Teensy_3_1.D12
  N6: WIZ820io1.nRESET, Teensy_3_1.D9
  N7: M1.SCL, OLED_I2C1.SCK, Teensy_3_1.A5/D19
  N8: M1.SDA, OLED_I2C1.SDA, Teensy_3_1.A4/D18
  N9: U1.B#2, Teensy_3_1.D3
  N10: U1.R, Teensy_3_1.A0/D14
  N11: U1.G, Teensy_3_1.A1/D15
  N12: U1.SW, Teensy_3_1.A8/D22

custom parts:
  Adafruit MAX4466 Electret Microphone Amplifier: Add an ear to your project with this well-designed electret microphone amplifier. This fully assembled and tested board comes with a 20-20KHz electret microphone soldered on. For the amplification, we use the Maxim MAX4466, an op-amp specifically designed for this delicate task! The amplifier has excellent power supply noise rejection, so this amplifier sounds really good and isn't nearly as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
  BMP280: Temperature Humidity Barometric presure Sensor, I2C
  ENCODER_RGB: SparkFun RGB rotary Encoder
